// Logisim project Project4Given.circ as structural Verilog: 13 circuits, main circuit main
module main (
  input  [3:0] in_1,
  input  [3:0] in_2,
  input  [3:0] in_3,
  input  [3:0] in_4,
  input  [3:0] in_5
);

  wire CLK, keyboard_1_avail, keyboard_2_avail, keyboarddriver_1_read, keyboarddriver_2_read,
       pull_resistor_1_node, ttydriver_1_write, ttydriver_2_write, ttydriver_3_write, vpwbmonitor_1_last_fe;
  wire [3:0] vpwbmonitor_1_last_addr;
  wire [6:0] keyboard_1_data, keyboard_2_data, ttydriver_1_data, ttydriver_2_data, ttydriver_3_data;
  wire [7:0] vpwbmonitor_1_last_data;
  wire [24:0] vpwbmonitor_1_out_4;
  wire [31:0] vpwbmonitor_1_out_3;

  Clock clock_1 (.out(CLK));
  Keyboard keyboard_1 (
    .clk(CLK), .re(keyboarddriver_1_read), .avail(keyboard_1_avail), .data(keyboard_1_data));  // open: clr
  Keyboard keyboard_2 (
    .clk(CLK), .re(keyboarddriver_2_read), .avail(keyboard_2_avail), .data(keyboard_2_data));  // open: clr
  Pull_Resistor #(.pull(1)) pull_resistor_1 (.node(pull_resistor_1_node));
  KeyboardDriver keyboarddriver_1 (
    .DATA(keyboard_1_data), .DEST(in_1), .DR(keyboard_1_avail), .CLK(CLK), .RXIN(pull_resistor_1_node),
    .READ(keyboarddriver_1_read), .TXOUT(pull_resistor_1_node));
  KeyboardDriver keyboarddriver_2 (
    .DATA(keyboard_2_data), .DEST(in_3), .DR(keyboard_2_avail), .CLK(CLK), .RXIN(pull_resistor_1_node),
    .READ(keyboarddriver_2_read), .TXOUT(pull_resistor_1_node));
  // Probe on vpwbmonitor_1_out_3
  VPWBMonitor vpwbmonitor_1 (
    .RXIN(pull_resistor_1_node), .CLK(CLK), .LAST_FE(vpwbmonitor_1_last_fe),
    .LAST_ADDR(vpwbmonitor_1_last_addr), .LAST_DATA(vpwbmonitor_1_last_data), .out_3(vpwbmonitor_1_out_3),
    .out_4(vpwbmonitor_1_out_4));
  TTY tty_1 (.data(ttydriver_1_data), .clk(CLK), .we(ttydriver_1_write));  // open: clr
  TTYDriver ttydriver_1 (
    .RXIN(pull_resistor_1_node), .CLK(CLK), .TTY_ADDR(in_2), .TXOUT(pull_resistor_1_node),
    .WRITE(ttydriver_1_write), .DATA(ttydriver_1_data));
  TTY tty_2 (.data(ttydriver_2_data), .clk(CLK), .we(ttydriver_2_write));  // open: clr
  TTYDriver ttydriver_2 (
    .RXIN(pull_resistor_1_node), .CLK(CLK), .TTY_ADDR(in_4), .TXOUT(pull_resistor_1_node),
    .WRITE(ttydriver_2_write), .DATA(ttydriver_2_data));
  TTY tty_3 (.data(ttydriver_3_data), .clk(CLK), .we(ttydriver_3_write));  // open: clr
  TTYDriver ttydriver_3 (
    .RXIN(pull_resistor_1_node), .CLK(CLK), .TTY_ADDR(in_5), .TXOUT(pull_resistor_1_node),
    .WRITE(ttydriver_3_write), .DATA(ttydriver_3_data));
  // Probe on vpwbmonitor_1_out_4
  // Probe on vpwbmonitor_1_last_fe
  // Probe on vpwbmonitor_1_last_addr
  // Probe on vpwbmonitor_1_last_data
endmodule

module KeyboardDriver (
  input  DR,
  input  [6:0] DATA,
  input  RXIN,
  input  [3:0] DEST,
  input  CLK,
  output TXOUT,
  output READ
);

  wire ADDR, and_1_out, CHKDR, CS, JUMP, O, or_1_out, txrxd_1_din, vpwbcontroller_1_ser_out, W;
  wire [5:5] rom_1_data;
  wire [7:0] NPC, PC, PCPLUS1, PCTARGET;
  wire [11:0] multiplexer_1_out;

  Register register_1 (.D(NPC), .en(1'b1), .clk(CLK), .Q(PC));  // open: clr
  Adder adder_1 (.a(8'h1), .b(PC), .out(PCPLUS1));  // open: cin, cout
  ROM #(.dataWidth(16)) rom_1 (.addr(PC), .data({PCTARGET, JUMP, CHKDR, rom_1_data[5], READ, ADDR, O, W, CS}));
  Multiplexer #(.width(12)) multiplexer_1 (.in0(12'h1), .in1({DEST, 1'b0, DATA}), .out(multiplexer_1_out), .sel(ADDR));
  VPWBController vpwbcontroller_1 (
    .O(O), .ADDR(ADDR), .DATAIN(multiplexer_1_out), .CS(CS), .W(W), .CLK(CLK), .SER_IN(txrxd_1_din),
    .SER_OUT(vpwbcontroller_1_ser_out));  // open: I, DATAOUT
  and and_1 (and_1_out, CHKDR, DR);
  or or_1 (or_1_out, and_1_out, JUMP);
  Multiplexer #(.width(8)) multiplexer_2 (.in0(PCPLUS1), .in1(PCTARGET), .out(NPC), .sel(or_1_out));
  TXRXD txrxd_1 (.DOUT(vpwbcontroller_1_ser_out), .RXIN(RXIN), .DIN(txrxd_1_din), .TXOUT(TXOUT));

  // Other names for the same wires on the sheet: DATA_t[6:0] = DATA

  // Notes on the sheet:
  //   contents of rom_1 (hex, n*v repeats v):
  //   7 4 7 547 387 1c 387
endmodule

module TTYDriver (
  input  RXIN,
  input  [3:0] TTY_ADDR,
  input  CLK,
  output [6:0] DATA,
  output TXOUT,
  output WRITE
);

  wire ADDR, and_1_out, CHKDR, comparator_1_eq, CS, DR, JUMP, not_1_out, O, or_1_out, txrxd_1_din,
       vpwbcontroller_1_ser_out, W, WRITE_TTY;
  wire [5:5] rom_1_data;
  wire [7:0] NPC, PC, PCPLUS1, PCTARGET;
  wire [11:0] DATAOUT, register_2_q;

  Register register_1 (.D(NPC), .en(1'b1), .clk(CLK), .Q(PC));  // open: clr
  Adder adder_1 (.a(8'h1), .b(PC), .out(PCPLUS1));  // open: cin, cout
  ROM #(.dataWidth(16)) rom_1 (.addr(PC), .data({PCTARGET, JUMP, CHKDR, rom_1_data[5], WRITE_TTY, ADDR, O, W, CS}));
  Register #(.width(12)) register_2 (
    .D(DATAOUT), .en(not_1_out), .clk(CLK), .Q({register_2_q[11:2], DR, register_2_q[0]}));  // open: clr
  not not_1 (not_1_out, O);
  and and_1 (and_1_out, CHKDR, DR);
  VPWBController vpwbcontroller_1 (
    .O(O), .ADDR(ADDR), .DATAIN({4'b1111, TTY_ADDR, 4'b0001}), .CS(CS), .W(W), .CLK(CLK),
    .SER_IN(txrxd_1_din), .DATAOUT(DATAOUT), .SER_OUT(vpwbcontroller_1_ser_out));  // open: I
  Multiplexer #(.width(8)) multiplexer_1 (.in0(PCPLUS1), .in1(PCTARGET), .out(NPC), .sel(or_1_out));
  or or_1 (or_1_out, and_1_out, JUMP);
  Comparator #(.mode("unsigned"), .width(4)) comparator_1 (
    .a(register_2_q[11:8]), .b(TTY_ADDR), .eq(comparator_1_eq));  // open: gt, lt
  and and_2 (WRITE, comparator_1_eq, WRITE_TTY);
  Multiplexer #(.width(7)) multiplexer_2 (
    .in0({7{1'b0}}), .in1({register_2_q[6:2], DR, register_2_q[0]}), .out(DATA), .sel(WRITE));
  TXRXD txrxd_1 (.DOUT(vpwbcontroller_1_ser_out), .RXIN(RXIN), .DIN(txrxd_1_din), .TXOUT(TXOUT));

  // Other names for the same wires on the sheet: CHAR[6:0] = DATA

  // Notes on the sheet:
  //   contents of rom_1 (hex, n*v repeats v):
  //   7 4 7 2 647 87 a 17 87
endmodule

module VPWBMonitor (
  input  RXIN,
  input  CLK,
  output [31:0] out_3,
  output [24:0] out_4,
  output LAST_FE,
  output [3:0] LAST_ADDR,
  output [7:0] LAST_DATA
);

  wire B0_ERR, B1_ERR, B2_ERR, B3_ERR, B4_ERR, B5_ERR, B6_ERR, B7_ERR, B8_ERR, B9_ERR, BA_ERR, BB_ERR,
       FOUND_IDLE, I4, I5, I6, I7, I8, I9, I10, I11, I12, I13, I14, I15, I16, I17, I18, I19, I20, I21, I22,
       I23, I24, I25, I26, I27, I28, I29, NEW_IDLE, not_7_out;
  wire [0:0] not_1_out, not_2_out, not_9_out, not_10_out, not_15_out, not_16_out, shifter_1_out_3,
       shifter_2_out_3, shifter_3_out_3, shifter_6_out_3, shifter_7_out_3, shifter_8_out_3, shifter_10_out_3,
       shifter_11_out_3, shifter_12_out_3;
  wire [1:0] shifter_1_out, shifter_2_out, shifter_3_out, shifter_6_out, shifter_7_out, shifter_8_out,
       shifter_10_out, shifter_11_out, shifter_12_out;
  wire [4:0] FRAME_LENGTH, priority_encoder_1_out;
  wire [5:0] subtractor_1_out, subtractor_2_out;
  wire [9:0] shifter_12_out_2;
  wire [10:0] shifter_11_out_2;
  wire [11:0] shifter_10_out_2, shifter_13_out;
  wire [13:0] shifter_8_out_2;
  wire [14:0] shifter_7_out_2;
  wire [15:0] shifter_6_out_2, shifter_9_out;
  wire [17:0] shifter_3_out_2;
  wire [18:0] shifter_2_out_2;
  wire [19:0] shifter_1_out_2, shifter_4_out;
  wire [24:0] and_6_out, not_8_out;
  wire [25:0] shifter_5_out;

  not not_1 (not_1_out[0], LAST_DATA[1]);
  not not_2 (not_2_out[0], LAST_DATA[3]);
  Subtractor #(.width(6)) subtractor_1 (
    .a(6'b011001), .b({1'b0, FRAME_LENGTH}), .out(subtractor_1_out));  // open: bin, bout
  Shifter #(.shift("lr"), .width(23)) shifter_1 (
    .in(out_4[24:2]), .\dist ({4'b0000, LAST_DATA[0]}),
    .out({shifter_1_out_2, shifter_1_out, shifter_1_out_3[0]}));
  Shifter #(.shift("lr"), .width(22)) shifter_2 (
    .in({shifter_1_out_2, shifter_1_out}), .\dist ({4'b0000, not_1_out[0]}),
    .out({shifter_2_out_2, shifter_2_out, shifter_2_out_3[0]}));
  Shifter #(.shift("lr"), .width(21)) shifter_3 (
    .in({shifter_2_out_2, shifter_2_out}), .\dist ({4'b0000, LAST_DATA[2]}),
    .out({shifter_3_out_2, shifter_3_out, shifter_3_out_3[0]}));
  Shifter #(.shift("lr"), .width(20)) shifter_4 (
    .in({shifter_3_out_2, shifter_3_out}), .\dist ({4'b0000, not_2_out[0]}), .out(shifter_4_out));
  // Probe on shifter_5_out
  and and_1 (B0_ERR, ~out_4[1], ~out_4[2], ~out_4[3]);  // AND_Gate
  not not_3 (LAST_DATA[0], out_4[2]);
  and and_2 (B1_ERR, shifter_1_out_3[0], shifter_1_out[0], shifter_1_out[1]);
  not not_4 (LAST_DATA[1], shifter_1_out[0]);
  and and_3 (B2_ERR, ~shifter_2_out_3[0], ~shifter_2_out[0], ~shifter_2_out[1]);  // AND_Gate
  not not_5 (LAST_DATA[2], shifter_2_out[0]);
  and and_4 (B3_ERR, shifter_3_out_3[0], shifter_3_out[0], shifter_3_out[1]);
  not not_6 (LAST_DATA[3], shifter_3_out[0]);
  not not_7 (not_7_out, RXIN);
  Shift_Register #(.length(32)) shift_register_1 (
    .shift(1'b1), .in(not_7_out), .clk(CLK), .out(out_3[31]), .q0(out_3[0]), .q1(out_3[1]), .q2(out_3[2]),
    .q3(out_3[3]), .q4(out_3[4]), .q5(out_3[5]), .q6(out_3[6]), .q7(out_3[7]), .q8(out_3[8]), .q9(out_3[9]),
    .q10(out_3[10]), .q11(out_3[11]), .q12(out_3[12]), .q13(out_3[13]), .q14(out_3[14]), .q15(out_3[15]),
    .q16(out_3[16]), .q17(out_3[17]), .q18(out_3[18]), .q19(out_3[19]), .q20(out_3[20]), .q21(out_3[21]),
    .q22(out_3[22]), .q23(out_3[23]), .q24(out_3[24]), .q25(out_3[25]), .q26(out_3[26]), .q27(out_3[27]),
    .q28(out_3[28]), .q29(out_3[29]), .q30(out_3[30]));  // open: load, clr, d0, d1, d2, d3, d4, d5, d6, d7, d8, d9, d10, d11, d12, d13, d14, d15, d16, d17, d18, d19, d20, d21, d22, d23, d24, d25, d26, d27, d28, d29, d30, d31, q31
  and and_5 (NEW_IDLE, ~out_3[0], ~out_3[1], ~out_3[2], out_3[3]);  // AND_Gate
  assign not_8_out = ~shifter_5_out[24:0];  // NOT_Gate not_8, 25 bits wide
  Shifter #(.shift("ar"), .width(26)) shifter_5 (.in(26'h2000000), .\dist (subtractor_1_out[4:0]), .out(shifter_5_out));
  not not_9 (not_9_out[0], LAST_DATA[5]);
  not not_10 (not_10_out[0], LAST_DATA[7]);
  Shifter #(.shift("lr"), .width(19)) shifter_6 (
    .in(shifter_4_out[19:1]), .\dist ({4'b0000, LAST_DATA[4]}),
    .out({shifter_6_out_2, shifter_6_out, shifter_6_out_3[0]}));
  Shifter #(.shift("lr"), .width(18)) shifter_7 (
    .in({shifter_6_out_2, shifter_6_out}), .\dist ({4'b0000, not_9_out[0]}),
    .out({shifter_7_out_2, shifter_7_out, shifter_7_out_3[0]}));
  Shifter #(.shift("lr"), .width(17)) shifter_8 (
    .in({shifter_7_out_2, shifter_7_out}), .\dist ({4'b0000, LAST_DATA[6]}),
    .out({shifter_8_out_2, shifter_8_out, shifter_8_out_3[0]}));
  Shifter #(.shift("lr"), .width(16)) shifter_9 (
    .in({shifter_8_out_2, shifter_8_out}), .\dist ({3'b000, not_10_out[0]}), .out(shifter_9_out));
  // Probe on and_6_out
  Register #(.width(25)) register_1 (.D(and_6_out), .en(NEW_IDLE), .clk(CLK), .Q(out_4));  // open: clr
  assign and_6_out = out_3[27:3] & not_8_out;  // AND_Gate and_6, 25 bits wide
  and and_7 (B4_ERR, ~shifter_4_out[0], ~shifter_4_out[1], ~shifter_4_out[2]);  // AND_Gate
  not not_11 (LAST_DATA[4], shifter_4_out[1]);
  and and_8 (B5_ERR, shifter_6_out_3[0], shifter_6_out[0], shifter_6_out[1]);
  not not_12 (LAST_DATA[5], shifter_6_out[0]);
  and and_9 (B6_ERR, ~shifter_7_out_3[0], ~shifter_7_out[0], ~shifter_7_out[1]);  // AND_Gate
  not not_13 (LAST_DATA[6], shifter_7_out[0]);
  and and_10 (B7_ERR, shifter_8_out_3[0], shifter_8_out[0], shifter_8_out[1]);
  not not_14 (LAST_DATA[7], shifter_8_out[0]);
  not not_15 (not_15_out[0], LAST_ADDR[1]);
  not not_16 (not_16_out[0], LAST_ADDR[3]);
  and and_11 (B8_ERR, ~shifter_9_out[0], ~shifter_9_out[1], ~shifter_9_out[2]);  // AND_Gate
  not not_17 (LAST_ADDR[0], shifter_9_out[1]);
  Shifter #(.shift("lr"), .width(15)) shifter_10 (
    .in(shifter_9_out[15:1]), .\dist ({3'b000, LAST_ADDR[0]}),
    .out({shifter_10_out_2, shifter_10_out, shifter_10_out_3[0]}));
  and and_12 (B9_ERR, shifter_10_out_3[0], shifter_10_out[0], shifter_10_out[1]);
  not not_18 (LAST_ADDR[1], shifter_10_out[0]);
  Shifter #(.shift("lr"), .width(14)) shifter_11 (
    .in({shifter_10_out_2, shifter_10_out}), .\dist ({3'b000, not_15_out[0]}),
    .out({shifter_11_out_2, shifter_11_out, shifter_11_out_3[0]}));
  and and_13 (BA_ERR, ~shifter_11_out_3[0], ~shifter_11_out[0], ~shifter_11_out[1]);  // AND_Gate
  not not_19 (LAST_ADDR[2], shifter_11_out[0]);
  Shifter #(.shift("lr"), .width(13)) shifter_12 (
    .in({shifter_11_out_2, shifter_11_out}), .\dist ({3'b000, LAST_ADDR[2]}),
    .out({shifter_12_out_2, shifter_12_out, shifter_12_out_3[0]}));
  and and_14 (BB_ERR, shifter_12_out_3[0], shifter_12_out[0], shifter_12_out[1]);
  not not_20 (LAST_ADDR[3], shifter_12_out[0]);
  Shifter #(.shift("lr"), .width(12)) shifter_13 (
    .in({shifter_12_out_2, shifter_12_out}), .\dist ({3'b000, not_16_out[0]}), .out(shifter_13_out));
  and and_15 (I29, ~out_3[31], ~out_3[30], ~out_3[29]);  // AND_Gate
  and and_16 (I28, ~out_3[30], ~out_3[29], ~out_3[28]);  // AND_Gate
  and and_17 (I27, ~out_3[29], ~out_3[28], ~out_3[27]);  // AND_Gate
  and and_18 (I26, ~out_3[28], ~out_3[27], ~out_3[26]);  // AND_Gate
  and and_19 (I24, ~out_3[26], ~out_3[25], ~out_3[24]);  // AND_Gate
  and and_20 (I23, ~out_3[25], ~out_3[24], ~out_3[23]);  // AND_Gate
  and and_21 (I25, ~out_3[27], ~out_3[26], ~out_3[25]);  // AND_Gate
  or or_1 (LAST_FE, out_4[1], B0_ERR, B1_ERR, B2_ERR, B3_ERR, B4_ERR, B5_ERR, B6_ERR, B7_ERR, B8_ERR, B9_ERR, BA_ERR, BB_ERR);
  and and_22 (I22, ~out_3[24], ~out_3[23], ~out_3[22]);  // AND_Gate
  and and_23 (I21, ~out_3[23], ~out_3[22], ~out_3[21]);  // AND_Gate
  and and_24 (I20, ~out_3[22], ~out_3[21], ~out_3[20]);  // AND_Gate
  and and_25 (I19, ~out_3[21], ~out_3[20], ~out_3[19]);  // AND_Gate
  and and_26 (I18, ~out_3[20], ~out_3[19], ~out_3[18]);  // AND_Gate
  and and_27 (I17, ~out_3[19], ~out_3[18], ~out_3[17]);  // AND_Gate
  and and_28 (I16, ~out_3[18], ~out_3[17], ~out_3[16]);  // AND_Gate
  and and_29 (I15, ~out_3[17], ~out_3[16], ~out_3[15]);  // AND_Gate
  and and_30 (I14, ~out_3[16], ~out_3[15], ~out_3[14]);  // AND_Gate
  and and_31 (I13, ~out_3[15], ~out_3[14], ~out_3[13]);  // AND_Gate
  and and_32 (I12, ~out_3[14], ~out_3[13], ~out_3[12]);  // AND_Gate
  and and_33 (I11, ~out_3[13], ~out_3[12], ~out_3[11]);  // AND_Gate
  and and_34 (I10, ~out_3[12], ~out_3[11], ~out_3[10]);  // AND_Gate
  and and_35 (I9, ~out_3[11], ~out_3[10], ~out_3[9]);  // AND_Gate
  and and_36 (I8, ~out_3[10], ~out_3[9], ~out_3[8]);  // AND_Gate
  and and_37 (I7, ~out_3[9], ~out_3[8], ~out_3[7]);  // AND_Gate
  and and_38 (I6, ~out_3[8], ~out_3[7], ~out_3[6]);  // AND_Gate
  and and_39 (I5, ~out_3[7], ~out_3[6], ~out_3[5]);  // AND_Gate
  and and_40 (I4, ~out_3[6], ~out_3[5], ~out_3[4]);  // AND_Gate
  Priority_Encoder #(.select(5)) priority_encoder_1 (
    .in0(I29), .in1(I28), .in2(I27), .in3(I26), .in4(I25), .in5(I24), .in6(I23), .in7(I22), .in8(I21),
    .in9(I20), .in10(I19), .in11(I18), .in12(I17), .in13(I16), .in14(I15), .in15(I14), .in16(I13),
    .in17(I12), .in18(I11), .in19(I10), .in20(I9), .in21(I8), .in22(I7), .in23(I6), .in24(I5), .in25(I4),
    .in26(1'b0), .in27(1'b0), .in28(1'b0), .in29(1'b0), .in30(1'b0), .in31(1'b0),
    .out(priority_encoder_1_out), .gs(FOUND_IDLE));  // open: en_out, en_in
  Subtractor #(.width(6)) subtractor_2 (
    .a(6'b011010), .b({1'b0, priority_encoder_1_out}), .out(subtractor_2_out));  // open: bin, bout
  Multiplexer #(.width(5)) multiplexer_1 (
    .in0({5{1'b0}}), .in1(subtractor_2_out[4:0]), .out(FRAME_LENGTH), .sel(FOUND_IDLE));

  // Other names for the same wires on the sheet: LAST_FRAME[24:0] = out_4; HIST[31:0] = out_3; B8 = LAST_ADDR[0];
  //   B9 = LAST_ADDR[1]; BA = LAST_ADDR[2]; BB = LAST_ADDR[3]; B0 = LAST_DATA[0]; B1 = LAST_DATA[1];
  //   B2 = LAST_DATA[2]; B3 = LAST_DATA[3]; B4 = LAST_DATA[4]; B5 = LAST_DATA[5]; B6 = LAST_DATA[6];
  //   B7 = LAST_DATA[7]; EOF_ERR = out_4[1]
endmodule

module TXRXD (
  input  DOUT,
  input  RXIN,
  output TXOUT,
  output DIN
);

  assign TXOUT = DOUT ? ~DOUT : 1'bz;  // Controlled_Inverter controlled_inverter_1
  not not_1 (DIN, RXIN);

  // Notes on the sheet:
  //   TXOUT: pull=down
endmodule

module VPWBController (
  input  CS,
  input  W,
  input  SER_IN,
  input  O,
  input  ADDR,
  input  [11:0] DATAIN,
  input  CLK,
  output SER_OUT,
  output I,
  output [11:0] DATAOUT
);

  wire DF, ENA, READ_DATA, READ_STATUS, vpwbrx_1_empty, vpwbrx_1_full, vpwbtx_1_full, WRITE_CONTROL,
       WRITE_DATA;
  wire [3:0] ADDR_BITS, CARE;
  wire [3:1] register_1_q;
  wire [3:2] Status_reg;
  wire [11:0] FRAME_OUT;

  not not_1 (Status_reg[2], vpwbtx_1_full);
  not not_2 (Status_reg[2], vpwbrx_1_full);
  not not_3 (DF, vpwbrx_1_empty);
  Register #(.width(12)) register_1 (
    .D(DATAIN), .en(WRITE_CONTROL), .clk(CLK), .Q({CARE, ADDR_BITS, register_1_q, ENA}));  // open: clr
  VPWBTX vpwbtx_1 (
    .FRAME_IN(DATAIN), .WRITE(WRITE_DATA), .ENA(ENA), .CLK(CLK), .SER_IN(SER_IN), .FULL(vpwbtx_1_full),
    .IDLE(Status_reg[3]), .SER_OUT(SER_OUT));
  VPWBRX vpwbrx_1 (
    .READ(READ_DATA), .ENA(ENA), .CARE(CARE), .CLK(CLK), .ADDR(ADDR_BITS), .SER_IN(SER_IN),
    .FRAME_OUT(FRAME_OUT), .FULL(vpwbrx_1_full), .EMPTY(vpwbrx_1_empty));
  Multiplexer #(.width(12)) multiplexer_1 (
    .in0({CARE, ADDR_BITS, Status_reg, DF, ENA}), .in1(FRAME_OUT), .out(DATAOUT), .sel(ADDR));
  and and_1 (READ_STATUS, ~CS, ~O, ~ADDR);  // AND_Gate
  and and_2 (WRITE_CONTROL, ~CS, ~W, ~ADDR);  // AND_Gate
  and and_3 (READ_DATA, ~CS, ~O, ADDR);  // AND_Gate
  and and_4 (WRITE_DATA, ~CS, ~W, ADDR);  // AND_Gate

  // Other names for the same wires on the sheet: Status_reg (some bits) = {CARE, ADDR_BITS, DF, ENA};
  //   TBNF = Status_reg[2]; TXI = Status_reg[3]
endmodule

module VPWBTX (
  input  [11:0] FRAME_IN,
  input  SER_IN,
  input  WRITE,
  input  ENA,
  input  CLK,
  output SER_OUT,
  output FULL,
  output IDLE
);

  wire and_1_out, and_2_out, and_3_out, and_4_out, and_5_out, and_6_out, ARBL, BITCMP, cs0, cs1, DQ, EMPTY,
       EVEN_BIT, FRAME_COM, IDLE_S, LOAD, LOAD_S, NENA, or_1_out, or_2_out, RELOAD, SHIFT, SROMT, Start_tx,
       TRAN_S, tx_idle, undriven, vpwbsro_1_ser_out, WAIT_S;
  wire [3:0] bit_count_q, Shift_t;
  wire [11:0] vpwbframequeue_1_frame_out;

  VPWBFrameQueue vpwbframequeue_1 (
    .FRAME_IN(FRAME_IN), .ENQUEUE(WRITE), .ENA(ENA), .CLK(CLK), .DEQUEUE(LOAD_S), .FULL(FULL),
    .FRAME_OUT(vpwbframequeue_1_frame_out), .EMPTY(EMPTY));
  and and_1 (and_1_out, IDLE_S, ~EMPTY, tx_idle);  // AND_Gate
  and and_2 (and_2_out, WAIT_S, tx_idle);
  and and_3 (and_3_out, TRAN_S, ARBL);
  and and_4 (and_4_out, WAIT_S, ~tx_idle);  // AND_Gate
  and and_5 (and_5_out, TRAN_S, ARBL);
  and and_6 (and_6_out, TRAN_S, ~ARBL, ~FRAME_COM, BITCMP);  // AND_Gate
  or or_1 (or_1_out, and_1_out, and_2_out, and_3_out, and_4_out);
  or or_2 (or_2_out, and_4_out, LOAD_S, and_5_out, and_6_out);
  not not_1 (NENA, ENA);
  and and_7 (LOAD_S, cs0, ~cs1);  // AND_Gate
  and and_8 (WAIT_S, cs0, cs1);
  VPWBSRO vpwbsro_1 (
    .LOAD(LOAD), .ENA(ENA), .PARA_IN(vpwbframequeue_1_frame_out), .CLK(CLK), .SHIFT(SHIFT), .RELOAD(ARBL),
    .EMPTY(SROMT), .SER_OUT(vpwbsro_1_ser_out), .BITSLEFT(Shift_t));
  Register #(.width(1)) register_1 (.D(or_1_out), .en(ENA), .clk(CLK), .Q(cs0), .clr(FRAME_COM));
  Register #(.width(1)) register_2 (.D(or_2_out), .en(ENA), .clk(CLK), .Q(cs1), .clr(FRAME_COM));
  and and_9 (IDLE_S, ~cs0, ~cs1);  // AND_Gate
  and and_10 (TRAN_S, ~cs0, cs1);  // AND_Gate
  and and_11 (IDLE, IDLE_S, EMPTY);
  and and_12 (SHIFT, BITCMP, ~SROMT);  // AND_Gate
  VPWBObserver vpwbobserver_1 (.ENA(ENA), .CLK(CLK), .RX(SER_IN), .IDLE(tx_idle));  // open: DIN, NEWBIT, out_7, out_8
  Counter #(.max('hf), .width(4)) bit_count (
    .count(SHIFT), .Q(bit_count_q), .up(undriven), .clk(CLK), .clr(FRAME_COM));  // open: load, D, carry
  or or_3 (LOAD, LOAD_S, RELOAD);
  and and_13 (RELOAD, WAIT_S, tx_idle);
  and and_14 (DQ, TRAN_S, FRAME_COM, ~ARBL);  // AND_Gate
  VPWBArbiter vpwbarbiter_1 (
    .DW(Start_tx), .EVENBIT(EVEN_BIT), .DOUT(vpwbsro_1_ser_out), .ENA(ENA), .CLK(CLK), .RX(SER_IN),
    .ARBL(ARBL), .BITCMP(BITCMP), .TX(SER_OUT));
  buf and_15 (Start_tx, TRAN_S);  // AND_Gate AND_Gate
  not not_2 (EVEN_BIT, bit_count_q[0]);
  and and_16 (FRAME_COM, ~bit_count_q[0], ~bit_count_q[1], bit_count_q[2], bit_count_q[3]);  // AND_Gate

  // Notes on the sheet:
  //   TX FIFO
  //   WAIT 
  //   TRANS > WAIT
  //   TRANS
  //   IDLE > LOAD
  //   WAIT > LOAD
  //   TRANS > WAIT
endmodule

module VPWBRX (
  input  [3:0] CARE,
  input  [3:0] ADDR,
  input  SER_IN,
  input  READ,
  input  ENA,
  input  CLK,
  output [11:0] FRAME_OUT,
  output FULL,
  output EMPTY
);

  wire and_3_out, and_4_out, and_5_out, and_6_out, DISCARD, DQ, ENQ, or_1_out, SRIFULL, vpwbobserver_1_din,
       vpwbobserver_1_idle, vpwbobserver_1_newbit;
  wire [11:0] vpwbsri_1_para_out;

  and and_1 (ENQ, SRIFULL, ~FULL);  // AND_Gate
  and and_2 (DQ, READ, ~EMPTY);  // AND_Gate
  VPWBSRI vpwbsri_1 (
    .READ(ENQ), .ENA(ENA), .CLK(CLK), .SER_IN(vpwbobserver_1_din), .NEWBIT(vpwbobserver_1_newbit),
    .CLEAR(or_1_out), .FULL(SRIFULL), .PARA_OUT(vpwbsri_1_para_out));
  or or_1 (or_1_out, vpwbobserver_1_idle, DISCARD);
  VPWBFrameQueue vpwbframequeue_1 (
    .FRAME_IN(vpwbsri_1_para_out), .ENQUEUE(ENQ), .ENA(ENA), .CLK(CLK), .DEQUEUE(DQ), .FULL(FULL),
    .FRAME_OUT(FRAME_OUT), .EMPTY(EMPTY));
  and and_3 (and_3_out, ~ADDR[3], CARE[3]);  // AND_Gate
  and and_4 (and_4_out, ~ADDR[2], CARE[2]);  // AND_Gate
  VPWBObserver vpwbobserver_1 (
    .ENA(ENA), .CLK(CLK), .RX(SER_IN), .DIN(vpwbobserver_1_din), .NEWBIT(vpwbobserver_1_newbit),
    .IDLE(vpwbobserver_1_idle));  // open: out_7, out_8
  or or_2 (DISCARD, and_3_out, and_4_out, and_5_out, and_6_out);
  and and_5 (and_5_out, ~ADDR[1], CARE[1]);  // AND_Gate
  and and_6 (and_6_out, ~ADDR[0], CARE[0]);  // AND_Gate

  // Other names for the same wires on the sheet: A0 = ADDR[0]; A1 = ADDR[1]; A2 = ADDR[2]; A3 = ADDR[3]; C0 = CARE[0];
  //   C1 = CARE[1]; C2 = CARE[2]; C3 = CARE[3]

  // Notes on the sheet:
  //   RX FIFO
  //   Inputs: SER_IN, CLK, ENA, READ, CARE, ADDR
  //   Outputs: FRAME_OUT, FULL, EMPTY
endmodule

module VPWBFrameQueue (
  input  [11:0] FRAME_IN,
  input  ENQUEUE,
  input  DEQUEUE,
  input  ENA,
  input  CLK,
  output [11:0] FRAME_OUT,
  output FULL,
  output EMPTY
);

  wire and_1_out, and_2_out, and_3_out, and_4_out, and_5_out, and_10_out, and_11_out, and_12_out, and_13_out,
       ENQDQ, ENQDQR0, ENQDQR1, ENQDQR2, ENQDQR3, NENA, R0, R0MUX, R1, R1MUX, R2, R2MUX, R3, R3MUX, REG_EN,
       REG_EN0, REG_EN1, REG_EN2, REG_EN3, XDQ, xor_1_out;
  wire [2:0] QTRACKER;
  wire [11:0] demultiplexer_1_out0, demultiplexer_1_out1, demultiplexer_1_out2, demultiplexer_1_out3,
       demultiplexer_1_out4, ENQ0, ENQ1, ENQ2, ENQ3, multiplexer_1_out, multiplexer_2_out, multiplexer_3_out,
       multiplexer_4_out, register_2_q, register_3_q, register_4_q;

  not not_1 (NENA, ENA);
  Decoder #(.select(3)) decoder_1 (
    .out0(R0), .out1(R1), .out2(R2), .out3(R3), .sel(QTRACKER));  // open: out4, out5, out6, out7, en
  Decoder #(.select(3)) decoder_2 (
    .out1(ENQDQR0), .out2(ENQDQR1), .out3(ENQDQR2), .out4(ENQDQR3), .sel(QTRACKER));  // open: out0, out5, out6, out7, en
  Multiplexer #(.width(12)) multiplexer_1 (.in0(ENQ0), .in1(register_2_q), .out(multiplexer_1_out), .sel(R0MUX));
  Multiplexer #(.width(12)) multiplexer_2 (.in0(ENQ1), .in1(register_3_q), .out(multiplexer_2_out), .sel(R1MUX));
  Multiplexer #(.width(12)) multiplexer_3 (.in0(ENQ2), .in1(register_4_q), .out(multiplexer_3_out), .sel(R2MUX));
  Multiplexer #(.width(12)) multiplexer_4 (.in0(ENQ3), .in1({12{1'b0}}), .out(multiplexer_4_out), .sel(R3MUX));
  Register #(.width(12)) register_1 (.D(multiplexer_1_out), .en(REG_EN0), .clk(CLK), .Q(FRAME_OUT), .clr(NENA));
  Register #(.width(12)) register_2 (.D(multiplexer_2_out), .en(REG_EN1), .clk(CLK), .Q(register_2_q), .clr(NENA));
  Register #(.width(12)) register_3 (.D(multiplexer_3_out), .en(REG_EN2), .clk(CLK), .Q(register_3_q), .clr(NENA));
  Register #(.width(12)) register_4 (.D(multiplexer_4_out), .en(REG_EN3), .clk(CLK), .Q(register_4_q), .clr(NENA));
  Demultiplexer #(.select(3), .width(12)) demultiplexer_1 (
    .out0(demultiplexer_1_out0), .out1(demultiplexer_1_out1), .out2(demultiplexer_1_out2),
    .out3(demultiplexer_1_out3), .out4(demultiplexer_1_out4), .in(FRAME_IN), .sel(QTRACKER));  // open: out5, out6, out7
  and and_1 (and_1_out, ENQUEUE, ~DEQUEUE);  // AND_Gate
  xor xor_1 (xor_1_out, ENQUEUE, DEQUEUE);
  and and_2 (and_2_out, REG_EN, R0);
  and and_3 (and_3_out, REG_EN, R1);
  and and_4 (and_4_out, REG_EN, R2);
  and and_5 (and_5_out, REG_EN, R3);
  Multiplexer #(.width(12)) multiplexer_5 (
    .in0(demultiplexer_1_out0), .in1(demultiplexer_1_out1), .out(ENQ0), .sel(ENQDQ));
  Multiplexer #(.width(12)) multiplexer_6 (
    .in0(demultiplexer_1_out1), .in1(demultiplexer_1_out2), .out(ENQ1), .sel(ENQDQ));
  Multiplexer #(.width(12)) multiplexer_7 (
    .in0(demultiplexer_1_out2), .in1(demultiplexer_1_out3), .out(ENQ2), .sel(ENQDQ));
  Multiplexer #(.width(12)) multiplexer_8 (
    .in0(demultiplexer_1_out3), .in1(demultiplexer_1_out4), .out(ENQ3), .sel(ENQDQ));
  Counter #(.max('h4), .ongoal("stay"), .width(3)) counter_1 (
    .count(xor_1_out), .Q(QTRACKER), .up(and_1_out), .clk(CLK), .clr(NENA));  // open: load, D, carry
  and and_6 (REG_EN, ENQUEUE, ~FULL);  // AND_Gate
  or or_1 (REG_EN0, and_2_out, DEQUEUE, ENQDQ);
  or or_2 (REG_EN1, and_3_out, DEQUEUE, ENQDQ);
  or or_3 (REG_EN2, and_4_out, DEQUEUE, ENQDQ);
  or or_4 (REG_EN3, and_5_out, DEQUEUE, ENQDQ);
  and and_7 (ENQDQ, ENQUEUE, DEQUEUE);
  and and_8 (EMPTY, ~QTRACKER[0], ~QTRACKER[1], ~QTRACKER[2]);  // AND_Gate
  and and_9 (FULL, ~QTRACKER[0], ~QTRACKER[1], QTRACKER[2]);  // AND_Gate
  and and_10 (and_10_out, ENQDQ, ~ENQDQR0);  // AND_Gate
  and and_11 (and_11_out, ENQDQ, ~ENQDQR1);  // AND_Gate
  and and_12 (and_12_out, ENQDQ, ~ENQDQR2);  // AND_Gate
  and and_13 (and_13_out, ENQDQ, ~ENQDQR3);  // AND_Gate
  and and_14 (XDQ, DEQUEUE, ~ENQUEUE);  // AND_Gate
  or or_5 (R0MUX, XDQ, and_10_out);
  or or_6 (R1MUX, XDQ, and_11_out);
  or or_7 (R2MUX, XDQ, and_12_out);
  or or_8 (R3MUX, XDQ, and_13_out);

  // Notes on the sheet:
  //   During ENQDQ
  //   Keeps track of where to ENQ
  //   Keeps track of where to overwrite 
  //   Head of the Q
  //   Inputs: DEQUEUE, CLK, ENA, FRAME_IN, ENQUEUE
  //   Outputs: FRAME_OUT, EMPTY, FULL
endmodule

module VPWBSRI (
  input  READ,
  input  SER_IN,
  input  NEWBIT,
  input  CLEAR,
  input  ENA,
  input  CLK,
  output FULL,
  output [11:0] PARA_OUT
);

  wire and_1_out, and_2_out, and_3_out, and_5_out, COUNTEN, NENA, or_1_out, RESET;
  wire [3:0] counter_1_q;
  wire [11:0] shift_register_1_out;

  Shift_Register #(.length(12)) shift_register_1 (
    .shift(NEWBIT), .in(SER_IN), .clk(CLK), .out(shift_register_1_out[0]), .clr(RESET),
    .q0(shift_register_1_out[11]), .q1(shift_register_1_out[10]), .q2(shift_register_1_out[9]),
    .q3(shift_register_1_out[8]), .q4(shift_register_1_out[7]), .q5(shift_register_1_out[6]),
    .q6(shift_register_1_out[5]), .q7(shift_register_1_out[4]), .q8(shift_register_1_out[3]),
    .q9(shift_register_1_out[2]), .q10(shift_register_1_out[1]));  // open: load, d0, d1, d2, d3, d4, d5, d6, d7, d8, d9, d10, d11, q11
  and and_1 (and_1_out, READ, FULL);
  Multiplexer #(.width(12)) multiplexer_1 (
    .in0({12{1'b0}}), .in1(shift_register_1_out), .out(PARA_OUT), .sel(and_1_out));
  not not_1 (NENA, ENA);
  Counter #(.max('hf), .width(4)) counter_1 (
    .count(COUNTEN), .Q(counter_1_q), .clk(CLK), .clr(or_1_out));  // open: load, D, carry, up
  or or_1 (or_1_out, RESET, and_3_out);
  or or_2 (RESET, CLEAR, NENA);
  and and_2 (and_2_out, counter_1_q[0], counter_1_q[1], ~counter_1_q[2], counter_1_q[3]);  // AND_Gate
  and and_3 (and_3_out, ~counter_1_q[0], ~counter_1_q[1], counter_1_q[2], counter_1_q[3]);  // AND_Gate
  and and_4 (COUNTEN, NEWBIT, ENA);
  D_Flip_Flop d_ff_1 (.D(and_5_out), .clk(CLK), .Q(FULL));  // open: Qn, preset, reset
  and and_5 (and_5_out, COUNTEN, and_2_out);
endmodule

module VPWBSRO (
  input  [11:0] PARA_IN,
  input  LOAD,
  input  SHIFT,
  input  RELOAD,
  input  ENA,
  input  CLK,
  output SER_OUT,
  output EMPTY,
  output [3:0] BITSLEFT
);

  wire NENA, or_1_out;
  wire [11:1] shift_register_1_q10;

  or or_1 (or_1_out, LOAD, RELOAD);
  Shift_Register #(.length(12)) shift_register_1 (
    .shift(SHIFT), .in(1'b0), .clk(CLK), .out(SER_OUT), .load(or_1_out), .clr(NENA), .d0(PARA_IN[11]),
    .q0(shift_register_1_q10[11]), .d1(PARA_IN[10]), .q1(shift_register_1_q10[10]), .d2(PARA_IN[9]),
    .q2(shift_register_1_q10[9]), .d3(PARA_IN[8]), .q3(shift_register_1_q10[8]), .d4(PARA_IN[7]),
    .q4(shift_register_1_q10[7]), .d5(PARA_IN[6]), .q5(shift_register_1_q10[6]), .d6(PARA_IN[5]),
    .q6(shift_register_1_q10[5]), .d7(PARA_IN[4]), .q7(shift_register_1_q10[4]), .d8(PARA_IN[3]),
    .q8(shift_register_1_q10[3]), .d9(PARA_IN[2]), .q9(shift_register_1_q10[2]), .d10(PARA_IN[1]),
    .q10(shift_register_1_q10[1]), .d11(PARA_IN[0]));  // open: q11
  BitAdder #(.width(12)) bitadder_1 (.in0({shift_register_1_q10, SER_OUT}), .out(BITSLEFT));
  not not_1 (NENA, ENA);
  nor nor_1 (EMPTY, BITSLEFT[0], BITSLEFT[1], BITSLEFT[2], BITSLEFT[3]);

  // Notes on the sheet:
  //   Inputs:
  //   Outputs: 
  //   SER_OUT, BITSLEFT, EMPTY
  //   SHIFT, RELOAD, CLK, ENA, LOAD, PARA_IN
endmodule

module VPWBArbiter (
  input  EVENBIT,
  input  DOUT,
  input  DW,
  input  RX,
  input  ENA,
  input  CLK,
  output TX,
  output ARBL,
  output BITCMP
);

  wire and_1_out, and_2_out, and_3_out, and_4_out, and_5_out, and_6_out, and_7_out, and_9_out, and_10_out,
       and_11_out, BIT1, BIT2, BUSIDLE, IDLE, NENA, or_1_out, or_2_out, register_1_q, register_2_q, SHORT,
       xnor_1_out, xor_1_out;

  not not_1 (NENA, ENA);
  and and_1 (and_1_out, SHORT, BIT1);
  or or_1 (or_1_out, and_1_out, IDLE, BIT2);
  and and_2 (and_2_out, IDLE, BUSIDLE, DW);
  and and_3 (and_3_out, BIT1, SHORT, DW);
  or or_2 (or_2_out, and_2_out, and_3_out, and_4_out);
  and and_4 (and_4_out, BIT2, DW);
  and and_5 (and_5_out, BIT1, ~SHORT, ~ARBL);  // AND_Gate
  and and_6 (and_6_out, or_1_out, ~DW);  // AND_Gate
  and and_7 (and_7_out, or_2_out, ~ARBL);  // AND_Gate
  D_Flip_Flop d_ff_1 (.D(xnor_1_out), .clk(CLK), .Qn(IDLE), .reset(NENA));  // open: Q, preset
  xnor xnor_1 (xnor_1_out, and_6_out, ARBL);
  D_Flip_Flop d_ff_2 (.D(and_7_out), .clk(CLK), .Q(BIT1), .reset(NENA));  // open: Qn, preset
  D_Flip_Flop d_ff_3 (.D(and_5_out), .clk(CLK), .Q(BIT2), .reset(NENA));  // open: Qn, preset
  and and_8 (ARBL, ~IDLE, xor_1_out);  // AND_Gate
  xor xor_1 (xor_1_out, TX, RX);
  Register #(.width(1)) register_1 (.D(DOUT), .en(DW), .clk(CLK), .Q(register_1_q), .clr(NENA));
  Register #(.width(1)) register_2 (.D(EVENBIT), .en(DW), .clk(CLK), .Q(register_2_q), .clr(NENA));
  and and_9 (and_9_out, BIT1, SHORT, ~ARBL);  // AND_Gate
  and and_10 (and_10_out, BIT2, ~ARBL);  // AND_Gate
  and and_11 (and_11_out, IDLE, BUSIDLE);
  VPWBObserver vpwbobserver_1 (.ENA(ENA), .CLK(CLK), .RX(RX), .IDLE(BUSIDLE));  // open: DIN, NEWBIT, out_7, out_8
  and and_12 (TX, ~IDLE, register_2_q);  // AND_Gate
  or or_3 (BITCMP, and_9_out, and_10_out, and_11_out);
  xnor xnor_2 (SHORT, register_1_q, register_2_q);
endmodule

module VPWBObserver (
  input  RX,
  input  ENA,
  input  CLK,
  output IDLE,
  output DIN,
  output NEWBIT,
  output [3:0] out_7,
  output [2:0] out_8
);

  wire and_1_out, and_2_out, ERR, NENA, or_1_out, PREV_IDLE, RX1, RX2, RX3, xnor_1_out, xor_1_out;

  D_Flip_Flop d_ff_1 (.D(RX), .clk(CLK), .Q(RX1), .reset(NENA));  // open: Qn, preset
  and and_1 (and_1_out, ERR, ~IDLE);  // AND_Gate
  and and_2 (and_2_out, RX, RX1, RX2);
  ROM #(.addrWidth(4), .dataWidth(3)) rom_1 (.addr({RX, out_7[2:0]}), .data(out_8));
  D_Flip_Flop d_ff_2 (.D(RX1), .clk(CLK), .Q(RX2), .reset(NENA));  // open: Qn, preset
  D_Flip_Flop d_ff_3 (.D(or_1_out), .clk(CLK), .Q(ERR), .reset(NENA));  // open: Qn, preset
  or or_1 (or_1_out, and_1_out, and_2_out);
  D_Flip_Flop d_ff_4 (.D(RX2), .clk(CLK), .Q(RX3), .reset(NENA));  // open: Qn, preset
  Register #(.width(3)) register_1 (.D(out_8), .en(ENA), .clk(CLK));  // open: Q, clr
  xor xor_1 (xor_1_out, RX, RX1);
  nor nor_1 (IDLE, RX, RX1, RX2);
  nor nor_2 (PREV_IDLE, RX1, RX2, RX3);
  not not_1 (NENA, ENA);
  and and_3 (NEWBIT, xor_1_out, ~ERR, ~PREV_IDLE);  // AND_Gate
  xor xor_2 (DIN, RX1, xnor_1_out);
  xnor xnor_1 (xnor_1_out, RX1, RX2);

  assign out_7[3] = RX;

  // Other names for the same wires on the sheet: S0 = out_7[0]; S1 = out_7[1]; S2 = out_7[2]

  // Notes on the sheet:
  //   IDLE - 000
  //   B0 - 0 after 1
  //   B00 - 2 0 since 1
  //   B1 - 1 after 0
  //   B11 - 2 1 since 0
  //   E1 - 3 1 since 0/1 from E
  //   E0 - 0 from E1
  //   E00 - 2 0 from E1
  //   contents of rom_1 (hex, n*v repeats v):
  //   0 2 0 1 1 6 7 0 3 3 3 4 4*5
  //   Shift Register 
  //   State + RX
  //   Next State
  //   Current State
endmodule
